// Logisim project P1.circ as structural Verilog: 1 circuit, main circuit main
module main (
  input  x,
  input  y,
  input  x_2,
  input  y_2,
  input  x_3,
  input  X_4,
  input  Y_3,
  input  in_8,
  input  in_9,
  output X_Y,
  output X_Y_2,
  output X_5,
  output X_Y_3,
  output X_Y_4
);

  not not_1 (X_5, x_3);
  and and_1 (X_Y, x, y);
  or or_1 (X_Y_2, x_2, y_2);
  xor xor_1 (X_Y_3, X_4, Y_3);
  xnor xnor_1 (X_Y_4, in_8, in_9);
endmodule
