// Logisim project P13.circ as structural Verilog: 4 circuits, main circuit main
module main (
  input  a,
  input  b,
  input  b_in,
  output difference,
  output out_5
);

  wire and_1_out, and_2_out, not_1_out, not_2_out, xor_1_out;

  xor xor_1 (xor_1_out, a, b);
  not not_1 (not_1_out, a);
  not not_2 (not_2_out, xor_1_out);
  and and_1 (and_1_out, not_1_out, b);
  and and_2 (and_2_out, not_2_out, b_in);
  xor xor_2 (difference, xor_1_out, b_in);
  or or_1 (out_5, and_2_out, and_1_out);

  // Notes on the sheet:
  //   b_out
endmodule

module D_A_B_C (
  input  ABC,
  input  D0,
  input  D1,
  input  D2,
  input  D3,
  input  D4,
  input  D5,
  input  D6,
  input  D7
);
endmodule

module F_A_B_C (
  input  A,
  input  B,
  input  C,
  output D0,
  output D1,
  output D2,
  output D3,
  output D4,
  output D5,
  output D6,
  output D7
);

  wire and_1_out, and_2_out, and_3_out, and_4_out, and_5_out, and_6_out, and_7_out, and_8_out, not_1_out,
       not_2_out, not_3_out, not_4_out, not_5_out, not_6_out, not_7_out, not_8_out, not_9_out, not_10_out,
       not_11_out, not_12_out;

  not not_1 (not_1_out, A);
  not not_2 (not_2_out, B);
  not not_3 (not_3_out, A);
  not not_4 (not_4_out, B);
  not not_5 (not_5_out, A);
  not not_6 (not_6_out, A);
  not not_7 (not_7_out, B);
  not not_8 (not_8_out, B);
  and and_1 (and_1_out, A, B);
  not not_9 (not_9_out, C);
  and and_2 (and_2_out, A, B);
  and and_3 (and_3_out, not_1_out, not_2_out);
  not not_10 (not_10_out, C);
  and and_4 (and_4_out, not_3_out, not_4_out);
  and and_5 (and_5_out, not_5_out, B);
  not not_11 (not_11_out, C);
  and and_6 (and_6_out, not_6_out, B);
  and and_7 (and_7_out, A, not_7_out);
  not not_12 (not_12_out, C);
  and and_8 (and_8_out, A, not_8_out);
  and and_9 (D6, and_1_out, not_9_out);
  and and_10 (D7, and_2_out, C);
  and and_11 (D0, and_3_out, not_10_out);
  and and_12 (D1, and_4_out, C);
  and and_13 (D2, and_5_out, not_11_out);
  and and_14 (D3, and_6_out, C);
  and and_15 (D4, and_7_out, not_12_out);
  and and_16 (D5, and_8_out, C);
endmodule

module F_A_B_C_2 (
  input  A,
  input  B,
  input  C,
  output D0,
  output D1,
  output D2,
  output D3,
  output D4,
  output D5,
  output D6,
  output D7
);
endmodule
