// Logisim project p10.circ as structural Verilog: 1 circuit, main circuit main
module main (
  input  a,
  input  b,
  input  b_in,
  output difference,
  output out_5
);

  wire and_1_out, and_2_out, not_1_out, not_2_out, xor_1_out;

  xor xor_1 (xor_1_out, a, b);
  not not_1 (not_1_out, a);
  not not_2 (not_2_out, xor_1_out);
  and and_1 (and_1_out, not_1_out, b);
  and and_2 (and_2_out, not_2_out, b_in);
  xor xor_2 (difference, xor_1_out, b_in);
  or or_1 (out_5, and_2_out, and_1_out);

  // Notes on the sheet:
  //   b_out
endmodule
