// Logisim project p16.circ as structural Verilog: 1 circuit, main circuit main
module main (
  input  in_1,
  input  in_2,
  input  in_3,
  input  in_4,
  input  in_5
);

  wire button_1_out, button_2_out, button_3_out, clock_1_out, clock_2_out, clock_3_out, d_ff_1_q, d_ff_2_q,
       d_ff_3_q, d_ff_4_q, d_ff_5_q, d_ff_6_q, d_ff_7_q, d_ff_8_q, d_ff_9_q, d_ff_10_q, d_ff_11_q, undriven,
       undriven_2, undriven_3, undriven_4;

  Clock clock_1 (.out(clock_1_out));
  Button button_1 (.out(button_1_out));
  Clock clock_2 (.out(clock_2_out));
  Button button_2 (.out(button_2_out));
  Clock clock_3 (.out(clock_3_out));
  Button button_3 (.out(button_3_out));
  D_Flip_Flop d_ff_1 (.clk(clock_3_out), .D(undriven), .Q(d_ff_1_q));  // open: Qn, preset, en, reset
  LED led_1 ();  // open: in
  D_Flip_Flop d_ff_2 (.clk(clock_1_out), .D(in_1), .Q(d_ff_2_q), .en(button_1_out));  // open: Qn, preset, reset
  D_Flip_Flop d_ff_3 (.clk(clock_2_out), .D(in_2), .Q(d_ff_3_q), .preset(button_2_out));  // open: Qn, en, reset
  D_Flip_Flop d_ff_4 (.clk(clock_3_out), .D(undriven_2), .Q(d_ff_4_q));  // open: Qn, preset, en, reset
  LED led_2 ();  // open: in
  D_Flip_Flop d_ff_5 (.clk(clock_1_out), .D(d_ff_2_q), .Q(d_ff_5_q), .en(button_1_out));  // open: Qn, preset, reset
  D_Flip_Flop d_ff_6 (.clk(clock_2_out), .D(d_ff_3_q), .Q(d_ff_6_q), .en(button_2_out));  // open: Qn, preset, reset
  D_Flip_Flop d_ff_7 (.clk(clock_3_out), .D(undriven_3), .Q(d_ff_7_q));  // open: Qn, preset, en, reset
  LED led_3 ();  // open: in
  D_Flip_Flop d_ff_8 (.clk(clock_1_out), .D(d_ff_5_q), .Q(d_ff_8_q), .en(button_1_out));  // open: Qn, preset, reset
  D_Flip_Flop d_ff_9 (.clk(clock_2_out), .D(d_ff_6_q), .Q(d_ff_9_q), .en(button_2_out));  // open: Qn, preset, reset
  D_Flip_Flop d_ff_10 (.clk(clock_1_out), .D(d_ff_8_q), .Q(d_ff_10_q), .reset(button_1_out));  // open: Qn, preset, en
  D_Flip_Flop d_ff_11 (.clk(clock_2_out), .D(d_ff_9_q), .Q(d_ff_11_q), .en(button_2_out));  // open: Qn, preset, reset
  D_Flip_Flop d_ff_12 (.clk(clock_3_out), .D(undriven_4), .en(button_3_out));  // open: Q, Qn, preset, reset
  LED led_4 (.in(d_ff_11_q));
  LED led_5 (.in(d_ff_10_q));

  // Notes on the sheet:
  //   siso
endmodule
