// Logisim project p18.circ as structural Verilog: 1 circuit, main circuit main
module main (
  input  control_variable,
  input  inpu
);

  wire and_1_out, and_2_out, and_3_out, and_4_out, clock_1_out, not_1_out, or_1_out, or_2_out, t_ff_1_q,
       t_ff_1_qn, t_ff_2_q, t_ff_2_qn;

  Clock clock_1 (.out(clock_1_out));
  T_Flip_Flop t_ff_1 (.clk(clock_1_out), .Q(t_ff_1_q), .Qn(t_ff_1_qn));  // open: T, preset, reset, en
  not not_1 (not_1_out, control_variable);
  and and_1 (and_1_out, not_1_out, t_ff_1_q);
  and and_2 (and_2_out, control_variable, t_ff_1_qn);
  or or_1 (or_1_out, and_1_out, and_2_out);
  T_Flip_Flop t_ff_2 (.clk(clock_1_out), .T(or_1_out), .Q(t_ff_2_q), .Qn(t_ff_2_qn));  // open: preset, reset, en
  and and_3 (and_3_out, and_1_out, t_ff_2_q);
  and and_4 (and_4_out, t_ff_2_qn, and_2_out);
  or or_2 (or_2_out, and_3_out, and_4_out);
  T_Flip_Flop t_ff_3 (.clk(clock_1_out), .T(or_2_out));  // open: Q, Qn, preset, reset, en

  // Notes on the sheet:
  //   clk
endmodule
