// Logisim project p2.circ as structural Verilog: 1 circuit, main circuit main
module main (
  input  x,
  input  y,
  input  x_2,
  input  y_2,
  input  x_3,
  output out_6,
  output out_7,
  output out_8
);

  wire nand_1_out, nand_2_out, nand_3_out;

  nand nand_1 (nand_1_out, x_2, x_2);
  nand nand_2 (nand_2_out, y_2, y_2);
  nand nand_3 (nand_3_out, x, y);
  nand nand_4 (out_8, x_3, x_3);
  nand nand_5 (out_6, nand_3_out, nand_3_out);
  nand nand_6 (out_7, nand_1_out, nand_2_out);

  // Notes on the sheet:
  //   '(x.y)
  //   'x
  //   'y
  //   'x
  //   x.y
  //   x+y
endmodule
