// Logisim project p4.circ as structural Verilog: 1 circuit, main circuit main
module main (
  input  in_1,
  input  in_2,
  input  in_3,
  input  in_4,
  input  in_5,
  input  in_6,
  input  in_7,
  input  in_8,
  output out_9,
  output out_10,
  output out_11,
  output out_12
);

  wire and_1_out, or_1_out;

  or or_1 (or_1_out, in_2, in_4);
  and and_1 (and_1_out, in_6, in_8);
  not not_1 (out_10, or_1_out);
  not not_2 (out_12, and_1_out);
  and and_2 (out_9, in_1, in_3);
  or or_2 (out_11, in_5, in_7);
endmodule
