// Logisim project p6.circ as structural Verilog: 1 circuit, main circuit main
module main (
  input  a,
  input  b,
  input  c,
  input  d,
  output f
);

  wire and_1_out, and_2_out, not_1_out, not_2_out;

  not not_1 (not_1_out, b);
  not not_2 (not_2_out, d);
  and and_1 (and_1_out, b, d);
  and and_2 (and_2_out, not_1_out, not_2_out);
  or or_1 (f, and_2_out, and_1_out);
endmodule
