// Logisim project p8.circ as structural Verilog: 1 circuit, main circuit main
module main (
  input  _1,
  input  b,
  input  c_in,
  output sum
);

  wire and_1_out, and_2_out, or_1_out, xor_1_out;

  xor xor_1 (xor_1_out, _1, b);
  and and_1 (and_1_out, b, _1);
  xor xor_2 (sum, xor_1_out, c_in);
  and and_2 (and_2_out, xor_1_out, c_in);
  or or_1 (or_1_out, and_2_out, and_1_out);

  // Notes on the sheet:
  //   a
endmodule
